# Fritzing sketch schematic (saved by Fritzing 0.9.4)
breadboards: 1

parts:
  Mod1 = Raspberry Pi Pico
  Q1 = Basic FET N-Channel [package="TO220 [THT]"]
  PART1 = SparkFun Soil Moisture Sensor [part_number=SEN-13322]
  R1 = Resistor [tolerance=±5% resistance=820 package=THT]
  LED1 = LED - 3mm [color="Orange (620nm)" package="3 mm [THT]"]

nets:
  N1: Mod1.pin_3, Mod1.pin_8, Mod1.pin_13, Mod1.pin_18, Mod1.pin_23, Mod1.pin_28, Mod1.pin_33, Mod1.pin_38, Q1.source, LED1.cathode
  N2: Mod1.pin_10, R1.Pin_0
  N3: Mod1.pin_29, Q1.gate
  N4: Mod1.pin_31, PART1.SIG
  N5: Mod1.pin_36, PART1.VCC
  N6: Q1.drain, PART1.GND
  N7: R1.Pin_1, LED1.anode

custom parts:
  Raspberry Pi Pico: Raspberry Pi Pico. Based around the RP2040 microcontroller the Pico is a low cost microcontroller device bringing Raspberry Pi quality, cost, and easy of use to the microcontroller space. Jan 2021, Split part in to two versions: tht (this one) and SMD. This one will drill holes for a .1 in header in pcb to allow plugging in the module as well as providing pads to solder the module to the top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
  SparkFun Soil Moisture Sensor: The SparkFun Soil Moisture Sensor is a simple breakout for measuring the moisture in soil and similar materials.
